# Fritzing sketch LDR_NODEMCU_RELE (saved by Fritzing 0.9.4)
breadboards: 1

parts:
  U1 = NodeMCU V1.0
  R1 = Photocell (LDR) [package=THT]
  R2 = Resistor [tolerance=±5% resistance=1k package="2512 [SMD]"]
  KY-1 = Keyes Relay [package=THT]
  Power_plug1 = Power plug [part_number=5v]

nets:
  N1: U1.D1, KY-1.signal
  N2: U1.3V3, R1.pin_0, KY-1.power
  GND: U1.GND, R2.Pin_1, KY-1.ground, Power_plug1.GND
  VIN: U1.Vin, Power_plug1.VCC
  N3: U1.A0, R1.pin_1, R2.Pin_0

custom parts:
  NodeMCU V1.0: ESP8266 based NodeMCU
  Keyes Relay: The Keyes 5V relay module is suitable for SCM development, home appliance control. It uses a 5V~12V TIL control signal which can control DC / AC signal.
